// Logisim project BFISA_VHDL.circ as structural Verilog: 4 circuits, main circuit main
module main (
  input  [7:0] Key
);

  wire and_1_out, and_2_out, and_3_out, and_4_out, Clk_out, comparator_1_gt, dbcr_pulse, decoder_hold,
       decoder_jump, decoder_loopback, decoder_memsrc, decoder_modmem, decoder_modptr, decoder_outp,
       Input_Valid_out, nor_1_out, nor_2_out, nor_3_out, nor_4_out, not_1_out, not_2_out, not_3_out,
       not_4_out, not_5_out, not_6_out, or_1_out, Reset_out, xor_1_out;
  wire [2:0] program_data;
  wire [6:0] mem_dout;
  wire [7:0] adder_3_out, multiplexer_3_out;
  wire [7:7] decoder_memop, mem_dout_2;
  wire [15:0] adder_1_out, adder_2_out, bit_extender_1_out, counter_1_q, multiplexer_1_out,
       multiplexer_2_out, PC_q, Pointer_q, register_1_q;
  wire [15:3] program_data_2;
  wire [15:15] decoder_ptrop;

  Clock Clk (.out(Clk_out));
  Button Reset (.out(Reset_out));
  Button Input_Valid (.out(Input_Valid_out));
  not not_1 (not_1_out, decoder_ptrop[15]);
  Comparator #(.width(16)) comparator_1 (
    .a(multiplexer_2_out), .b(register_1_q), .gt(comparator_1_gt));  // open: eq, lt
  Adder #(.width(16)) adder_1 (
    .a({16{decoder_ptrop[15]}}), .b(Pointer_q), .out(adder_1_out), .cin(not_1_out));  // open: cout
  Register #(.width(16)) register_1 (
    .D(multiplexer_2_out), .en(comparator_1_gt), .clk(Clk_out), .Q(register_1_q));  // open: clr
  Adder #(.width(16)) adder_2 (.a(PC_q), .b({16{1'b0}}), .out(adder_2_out), .cin(1'b1));  // open: cout
  Multiplexer #(.enable("false"), .width(16)) multiplexer_1 (
    .in0(adder_2_out), .in1(bit_extender_1_out), .out(multiplexer_1_out), .sel(and_1_out));
  and and_1 (and_1_out, xor_1_out, decoder_jump);
  xor xor_1 (xor_1_out, decoder_loopback, and_4_out);
  Debouncer dbcr (.Pulse(dbcr_pulse), .Buttn(Input_Valid_out), .Clk(Clk_out), .Rst(Reset_out));
  Decode decoder (
    .Opcode(program_data), .PtrOp(decoder_ptrop[15]), .MemOp(decoder_memop[7]), .LoopBack(decoder_loopback),
    .MemSrc(decoder_memsrc), .ModPtr(decoder_modptr), .Jump(decoder_jump), .Outp(decoder_outp),
    .ModMem(decoder_modmem), .Hold(decoder_hold));
  Register #(.width(16)) Pointer (.D(adder_1_out), .en(decoder_modptr), .clk(Clk_out), .Q(Pointer_q), .clr(Reset_out));
  or or_1 (or_1_out, dbcr_pulse, not_2_out);
  not not_2 (not_2_out, decoder_hold);
  Hex_Digit_Display hex_digit_display_1 (.value(register_1_q[15:12]));  // open: dp
  Register #(.width(16)) PC (.D(multiplexer_1_out), .en(or_1_out), .clk(Clk_out), .Q(PC_q), .clr(Reset_out));
  not not_3 (not_3_out, decoder_modptr);
  Multiplexer #(.enable("false"), .width(16)) multiplexer_2 (
    .in0(adder_1_out), .in1(Pointer_q), .out(multiplexer_2_out), .sel(not_3_out));
  Hex_Digit_Display hex_digit_display_2 (.value(register_1_q[11:8]));  // open: dp
  Hex_Digit_Display hex_digit_display_3 (.value(register_1_q[7:4]));  // open: dp
  ROM #(.addrWidth(16), .dataWidth(16)) \program  (.addr(PC_q), .data({program_data_2, program_data}));
  RAM #(.addrWidth(16)) mem (
    .addr(multiplexer_2_out), .we(decoder_modmem), .oe(1'b1), .clk(Clk_out), .din(multiplexer_3_out),
    .dout({mem_dout_2[7], mem_dout}));
  Hex_Digit_Display hex_digit_display_4 (.value(register_1_q[3:0]));  // open: dp
  not not_4 (not_4_out, Clk_out);
  TTY #(.cols(36), .rows(21)) tty_1 (.data(mem_dout), .clk(not_4_out), .we(decoder_outp), .clr(Reset_out));
  assign bit_extender_1_out = {{3{1'b0}}, program_data_2};  // Bit_Extender bit_extender_1
  not not_5 (not_5_out, decoder_memop[7]);
  Adder adder_3 (
    .a({mem_dout_2[7], mem_dout}), .b({8{decoder_memop[7]}}), .out(adder_3_out), .cin(not_5_out));  // open: cout
  nor nor_1 (nor_1_out, mem_dout[0], mem_dout[1]);
  and and_2 (and_2_out, nor_1_out, nor_2_out);
  nor nor_2 (nor_2_out, mem_dout[2], mem_dout[3]);
  nor nor_3 (nor_3_out, mem_dout[4], mem_dout[5]);
  and and_3 (and_3_out, nor_3_out, nor_4_out);
  nor nor_4 (nor_4_out, mem_dout[6], mem_dout_2[7]);
  Hex_Digit_Display hex_digit_display_5 (.value({mem_dout_2[7], mem_dout[6:4]}));  // open: dp
  Multiplexer #(.enable("false"), .width(8)) multiplexer_3 (
    .in0(adder_3_out), .in1(Key), .out(multiplexer_3_out), .sel(decoder_memsrc));
  Hex_Digit_Display hex_digit_display_6 (.value(multiplexer_3_out[7:4]));  // open: dp
  and and_4 (and_4_out, and_2_out, and_3_out);
  Hex_Digit_Display hex_digit_display_7 (.value(mem_dout[3:0]));  // open: dp
  Hex_Digit_Display hex_digit_display_8 (.value(multiplexer_3_out[3:0]));  // open: dp
  Hex_Digit_Display hex_digit_display_9 (.value(counter_1_q[15:12]));  // open: dp
  Counter #(.max('hffff), .width(16)) counter_1 (
    .clr(Reset_out), .load(1'b0), .up(1'b1), .count(not_6_out), .clk(Clk_out), .Q(counter_1_q));  // open: D, carry
  not not_6 (not_6_out, decoder_hold);
  Hex_Digit_Display hex_digit_display_10 (.value(counter_1_q[11:8]));  // open: dp
  Hex_Digit_Display hex_digit_display_11 (.value(counter_1_q[7:4]));  // open: dp
  Hex_Digit_Display hex_digit_display_12 (.value(counter_1_q[3:0]));  // open: dp

  // Notes on the sheet:
  //   contents of program (hex, n*v repeats v):
  //   0 1 13*2 144 3 0 2 2 0 0 0 5*2 0 2 2 0 2 6*1 7d 5*0 6*2 0 3 3 3 10*0 15*2 39c 2e4 9*0 28d 2 344 9*1
  //   2ed 9*0 3 285 2 414 8*0 404 3 3ed 0 3a5 9*1 4b4 9*1 45d 8*0 50c 3 4f5 2 7*1 5*2 684 3 634 3 9*0 2
  //   9*1 585 9*0 575 7*0 2 27*0 2 17*1 884 9*1 82d 0 0 0 8b4 3 89d 2 65ec 6*0 964 7*0 94c 3 935 0 0 8f5
  //   9*1 a04 9*1 9ad 7*0 a54 3 a3d 2 6*1 4*2 bbc 3 b6c 3 9*0 2 9*1 abd 9*0 aad 6*0 2 6*1 7*2 d6c 3 d1c 3
  //   9*0 2 9*1 c6d 9*0 c5d 6*0 2 16*1 e7c 9*1 e25 0 0 0 3dd4 eb4 3 e9d 6*0 10ac 7*0 fa4 3 6*1 2 6*0 f25
  //   6*1 1064 3 6*0 2 1 1 2 1 1 1 2 1 fd5 8*0 ee5 9*1 114c 9*1 10f5 9*0 138c 8*0 126c 3 7*1 2 7*0 11dd
  //   7*1 1344 3 7*0 2 1 1 2 1 1 1 2 1 1 12a5 8*0 1195 9*1 142c 9*1 13d5 7*0 14f4 3 7*1 2 7*0 1465 7*1
  //   15c4 3 7*0 2 1 1 2 5*1 152d 9*0 15*2 1904 16e4 9*0 168d 2 0 170c 3 16f5 0 172c 3 1715 0 174c 3 1735
  //   0 176c 3 1755 0 178c 3 1775 0 17ac 3 1795 0 17cc 3 17b5 0 17ec 3 17d5 0 180c 3 17f5 9*1 18ac 9*1
  //   1855 9*0 3 1685 2 196c 0 2 8*0 190d 9*1 1a0c 9*1 19b5 9*0 204c 0 3 4*0 1aec 3 4*1 2 4*0 1a8d 4*1
  //   1d3c 3 4*0 2 5*1 1c9c 3 0 0 1bcc 3 1 1 2 0 0 1b8d 1 1 1c44 3 0 0 2 0 0 2 4*1 1bdd 2 9*0 1b6d 8*1
  //   1d34 9*1 1cdd 1b0d 9*0 1ddc 9*0 1d85 9*1 1f3c 0 1ee4 3 9*0 2 9*1 1e35 10*1 1e25 0 1ff4 3 9*0 2 9*1
  //   1f45 1 2 8*0 1a55 9*1 22ec 0 20bc 3 20a5 1 3 4*0 2224 3 4*1 2 0 21c4 1 3 0 3 6*1 2 6*0 212d 1 21fc 3
  //   0 2 1 21cd 4*0 20ed 1 1 1 228c 3 0 0 0 2 1 1 1 223d 1 2 9*1 2095 9*0 2394 0 2 8*0 2335 9*1 2434 9*1
  //   23dd 9*0 2ae4 0 3 5*0 252c 3 5*1 2 5*0 24bd 5*1 27b4 3 5*0 2 6*1 2714 3 0 0 0 263c 3 1 1 1 2 0 0 0
  //   25ed 1 1 1 26bc 3 0 0 0 2 0 2 4*1 2655 2 9*0 25c5 8*1 27ac 9*1 2755 2555 9*0 2854 9*0 27fd 9*1 29c4
  //   0 0 2964 3 9*0 2 9*1 28b5 11*1 289d 0 0 2a84 3 9*0 2 9*1 29d5 1 1 2 8*0 247d 9*1 2d84 0 2b54 3 2b3d
  //   1 3 4*0 2cbc 3 4*1 2 0 2c5c 1 3 0 3 6*1 2 6*0 2bc5 1 2c94 3 0 2 1 2c65 4*0 2b85 1 1 1 2d24 3 0 0 0 2
  //   1 1 1 2cd5 1 2 9*1 2b2d 9*0 3084 4*0 3054 3 36*1 2 36*0 2df5 5*0 2dcd 9*1 3124 9*1 30cd 9*0 15*2
  //   338c 3244 9*0 31ed 9*1 3 9*1 3334 9*1 32dd 9*0 3 31e5 2 21*0 2 1 1 1 34b4 9*1 345d 9*0 3c74 0 0 0
  //   356c 3 1 1 1 3 0 0 0 351d 2 1 1 1 3824 3 0 0 0 3 0 3624 3 4*1 2 4*0 35c5 4*1 381c 3 4*0 2 13*1 373c
  //   9*1 36e5 4*0 3774 3 375d 2 5*0 37fc 9*0 37a5 0 2 1 3645 358d 2 4*0 38ac 3 4*1 3 4*0 384d 2 4*1 3b64
  //   3 4*0 3 1 3964 3 1 1 1 2 0 0 0 3915 1 1 1 3b5c 3 0 0 0 2 12*1 3a64 9*1 3a0d 0 0 0 3a94 3 3a7d 2 6*0
  //   3b24 9*0 3acd 0 3b44 3 3b2d 2 1 397d 38d5 2 0 3c2c 3 1 3be4 9*0 3b8d 8*1 3b75 8*0 34fd 9*1 3d14 9*1
  //   3cbd 7*1 3db4 3 0 2 0 0 0 3 4*1 3d4d 9*0 26*2 0 0 3f3c 3 4*1 2 4*0 3edd 4*1 3fd4 3 4*0 2 1 1 3fbc 3
  //   3fa5 1 1 3f5d 0 0 152c 7*1 2 1 40ac 3 1 2 4*0 2 1 1 40a4 3 408d 4035 0 415c 3 1 1 413c 3 0 2 0 0 0 3
  //   4*1 40d5 0 0 0 40b5 13*0 4264 0 0 41f4 3 41dd 0 4214 3 41fd 0 4234 3 421d 5*0 41c5 9*1 4304 9*1 42ad
  //   0 0 0 4334 3 431d 6*0 44c4 5*0 43f4 3 4*1 2 4*0 4395 4*1 447c 3 4*0 2 1 1 1 2 1 4415 8*0 4365 9*1
  //   4564 9*1 450d 9*0 46b4 0 0 4674 3 9*1 2 9*0 45c5 7*0 45ad 9*1 4754 9*1 46fd 9*0 15*2 4a94 4874 9*0
  //   481d 2 0 489c 3 4885 0 48bc 3 48a5 0 48dc 3 48c5 0 48fc 3 48e5 0 491c 3 4905 0 493c 3 4925 0 495c 3
  //   4945 0 497c 3 4965 0 499c 3 4985 9*1 4a3c 9*1 49e5 9*0 3 4815 2 4afc 0 2 8*0 4a9d 9*1 4b9c 9*1 4b45
  //   9*0 51fc 0 3 5*0 4c94 3 5*1 2 5*0 4c25 5*1 4eec 3 5*0 2 6*1 4e4c 3 0 0 4d8c 3 1 1 2 0 0 4d4d 1 1
  //   4df4 3 0 0 2 0 2 1 1 1 4d9d 2 9*0 4d2d 8*1 4ee4 9*1 4e8d 4cbd 9*0 4f8c 9*0 4f35 9*1 50ec 0 5094 3
  //   9*0 2 9*1 4fe5 10*1 4fd5 0 51a4 3 9*0 2 9*1 50f5 1 2 8*0 4be5 9*1 547c 0 526c 3 5255 1 3 0 0 0 53cc
  //   3 1 1 1 2 0 5374 1 3 0 3 7*1 2 7*0 52cd 1 53ac 3 0 2 1 537d 0 0 0 5295 1 1 541c 3 0 0 2 1 1 53dd 1 2
  //   9*1 5245 9*0 5654 6*0 556c 3 5*1 2 5*0 54fd 5*1 560c 3 5*0 2 4*1 2 1 5595 8*0 54c5 9*1 56f4 9*1 569d
  //   9*0 579c 0 2 8*0 573d 9*1 583c 9*1 57e5 9*0 5eac 0 3 5*0 5934 3 5*1 2 5*0 58c5 5*1 5b9c 3 5*0 2 6*1
  //   5afc 3 0 0 5a2c 3 1 1 2 0 0 59ed 1 1 5aa4 3 0 0 2 0 0 2 4*1 5a3d 2 9*0 59cd 8*1 5b94 9*1 5b3d 595d
  //   9*0 5c3c 9*0 5be5 9*1 5d9c 0 5d44 3 9*0 2 9*1 5c95 10*1 5c85 0 5e54 3 9*0 2 9*1 5da5 1 2 8*0 5885
  //   9*1 614c 0 5f1c 3 5f05 1 3 4*0 6084 3 4*1 2 0 6024 1 3 0 3 6*1 2 6*0 5f8d 1 605c 3 0 2 1 602d 4*0
  //   5f4d 1 1 1 60ec 3 0 0 0 2 1 1 1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
endmodule

module Decode (
  input  [2:0] Opcode,
  output PtrOp,
  output MemOp,
  output LoopBack,
  output MemSrc,
  output ModPtr,
  output Jump,
  output Outp,
  output ModMem,
  output Hold
);

  wire and_1_out, and_2_out, nor_3_out, nor_4_out, not_1_out;

  not not_1 (not_1_out, Opcode[2]);
  nor nor_1 (ModPtr, Opcode[1], Opcode[2]);
  nor nor_2 (Jump, Opcode[1], not_1_out);
  nor nor_3 (nor_3_out, Opcode[0], not_1_out);
  and and_1 (and_1_out, Opcode[1], not_1_out);
  and and_2 (and_2_out, Opcode[0], Opcode[1]);
  and and_3 (Outp, nor_3_out, Opcode[1]);
  nor nor_4 (nor_4_out, and_1_out, and_2_out);
  not not_2 (ModMem, nor_4_out);
  and and_4 (Hold, and_2_out, Opcode[2]);

  assign LoopBack = Opcode[0];
  assign MemOp = Opcode[0];
  assign MemSrc = Opcode[2];
  assign PtrOp = Opcode[0];
endmodule

module Debouncer (
  input  Buttn,
  input  Clk,
  input  Rst,
  output Pulse
);

  wire d_ff_1_q, d_ff_2_q, d_ff_3_q, d_ff_4_q, d_ff_5_q, d_ff_6_q, d_ff_7_q, d_ff_8_q, nand_1_out,
       nand_2_out, nor_1_out;

  D_Flip_Flop d_ff_1 (.D(Buttn), .clk(Clk), .Q(d_ff_1_q), .reset(Rst));  // open: Qn, preset
  D_Flip_Flop d_ff_2 (.D(d_ff_1_q), .clk(Clk), .Q(d_ff_2_q), .reset(Rst));  // open: Qn, preset
  D_Flip_Flop d_ff_3 (.D(d_ff_2_q), .clk(Clk), .Q(d_ff_3_q), .reset(Rst));  // open: Qn, preset
  D_Flip_Flop d_ff_4 (.D(d_ff_3_q), .clk(Clk), .Q(d_ff_4_q), .reset(Rst));  // open: Qn, preset
  D_Flip_Flop d_ff_5 (.D(d_ff_4_q), .clk(Clk), .Q(d_ff_5_q), .reset(Rst));  // open: Qn, preset
  D_Flip_Flop d_ff_6 (.D(d_ff_5_q), .clk(Clk), .Q(d_ff_6_q), .reset(Rst));  // open: Qn, preset
  D_Flip_Flop d_ff_7 (.D(d_ff_6_q), .clk(Clk), .Q(d_ff_7_q), .reset(Rst));  // open: Qn, preset
  D_Flip_Flop d_ff_8 (.D(d_ff_7_q), .clk(Clk), .Q(d_ff_8_q), .reset(Rst));  // open: Qn, preset
  nor nor_1 (nor_1_out, d_ff_8_q, d_ff_8_q);
  nand nand_1 (nand_1_out, d_ff_7_q, d_ff_6_q, d_ff_5_q, d_ff_4_q);
  nand nand_2 (nand_2_out, d_ff_3_q, d_ff_2_q, d_ff_1_q, nor_1_out);
  nor nor_2 (Pulse, nand_1_out, nand_2_out);
endmodule

module main_synth (
  input  Clk,
  input  Rst,
  input  Input_valid,
  input  [7:0] Key,
  output [6:0] Char_out,
  output out_enable
);

  wire and_1_out, and_2_out, and_3_out, and_4_out, dbcr_pulse, decoder_hold, decoder_jump, decoder_loopback,
       decoder_memsrc, decoder_modmem, decoder_modptr, nor_1_out, nor_2_out, nor_3_out, nor_4_out, not_1_out,
       not_2_out, not_3_out, not_4_out, or_1_out, or_2_out, xor_1_out;
  wire [2:0] program_data;
  wire [7:0] adder_3_out, multiplexer_3_out;
  wire [7:7] decoder_memop, mem_dout;
  wire [15:0] adder_1_out, adder_2_out, bit_extender_1_out, multiplexer_1_out, multiplexer_2_out, PC_q,
       Pointer_q;
  wire [15:3] program_data_2;
  wire [15:15] decoder_ptrop;

  not not_1 (not_1_out, decoder_ptrop[15]);
  Adder #(.width(16)) adder_1 (
    .a({16{decoder_ptrop[15]}}), .b(Pointer_q), .out(adder_1_out), .cin(not_1_out));  // open: cout
  Adder #(.width(16)) adder_2 (.a(PC_q), .b({16{1'b0}}), .out(adder_2_out), .cin(1'b1));  // open: cout
  Multiplexer #(.enable("false"), .width(16)) multiplexer_1 (
    .in0(adder_2_out), .in1(bit_extender_1_out), .out(multiplexer_1_out), .sel(and_1_out));
  and and_1 (and_1_out, xor_1_out, decoder_jump);
  xor xor_1 (xor_1_out, decoder_loopback, and_3_out);
  Debouncer dbcr (.Pulse(dbcr_pulse), .Buttn(Input_valid), .Clk(Clk), .Rst(Rst));
  Decode decoder (
    .Opcode(program_data), .PtrOp(decoder_ptrop[15]), .MemOp(decoder_memop[7]), .LoopBack(decoder_loopback),
    .MemSrc(decoder_memsrc), .ModPtr(decoder_modptr), .Jump(decoder_jump), .Outp(out_enable),
    .ModMem(decoder_modmem), .Hold(decoder_hold));
  Register #(.width(16)) Pointer (.D(adder_1_out), .en(decoder_modptr), .clk(Clk), .Q(Pointer_q), .clr(Rst));
  or or_1 (or_1_out, dbcr_pulse, not_2_out);
  not not_2 (not_2_out, decoder_hold);
  Register #(.width(16)) PC (.D(multiplexer_1_out), .en(or_1_out), .clk(Clk), .Q(PC_q), .clr(Rst));
  not not_3 (not_3_out, decoder_modptr);
  or or_2 (or_2_out, not_3_out, Clk);
  Multiplexer #(.enable("false"), .width(16)) multiplexer_2 (
    .in0(adder_1_out), .in1(Pointer_q), .out(multiplexer_2_out), .sel(or_2_out));
  ROM #(.addrWidth(16), .dataWidth(16)) \program  (.addr(PC_q), .data({program_data_2, program_data}));
  RAM #(.addrWidth(16)) mem (
    .addr(multiplexer_2_out), .we(decoder_modmem), .oe(1'b1), .clk(Clk), .din(multiplexer_3_out),
    .dout({mem_dout[7], Char_out}));
  assign bit_extender_1_out = {{3{1'b0}}, program_data_2};  // Bit_Extender bit_extender_1
  nor nor_1 (nor_1_out, mem_dout[7], Char_out[6]);
  nor nor_2 (nor_2_out, Char_out[5], Char_out[4]);
  nor nor_3 (nor_3_out, Char_out[3], Char_out[2]);
  nor nor_4 (nor_4_out, Char_out[1], Char_out[0]);
  not not_4 (not_4_out, decoder_memop[7]);
  Adder adder_3 (
    .a({mem_dout[7], Char_out}), .b({8{decoder_memop[7]}}), .out(adder_3_out), .cin(not_4_out));  // open: cout
  and and_2 (and_2_out, nor_1_out, nor_2_out);
  and and_3 (and_3_out, and_2_out, and_4_out);
  and and_4 (and_4_out, nor_3_out, nor_4_out);
  Multiplexer #(.enable("false"), .width(8)) multiplexer_3 (
    .in0(adder_3_out), .in1(Key), .out(multiplexer_3_out), .sel(decoder_memsrc));

  // Notes on the sheet:
  //   contents of program (hex, n*v repeats v):
  //   0 1 13*2 144 3 0 2 2 0 0 0 5*2 0 2 2 0 2 6*1 7d 5*0 6*2 0 3 3 3 10*0 15*2 39c 2e4 9*0 28d 2 344 9*1
  //   2ed 9*0 3 285 2 414 8*0 404 3 3ed 0 3a5 9*1 4b4 9*1 45d 8*0 50c 3 4f5 2 7*1 5*2 684 3 634 3 9*0 2
  //   9*1 585 9*0 575 7*0 2 27*0 2 17*1 884 9*1 82d 0 0 0 8b4 3 89d 2 65ec 6*0 964 7*0 94c 3 935 0 0 8f5
  //   9*1 a04 9*1 9ad 7*0 a54 3 a3d 2 6*1 4*2 bbc 3 b6c 3 9*0 2 9*1 abd 9*0 aad 6*0 2 6*1 7*2 d6c 3 d1c 3
  //   9*0 2 9*1 c6d 9*0 c5d 6*0 2 16*1 e7c 9*1 e25 0 0 0 3dd4 eb4 3 e9d 6*0 10ac 7*0 fa4 3 6*1 2 6*0 f25
  //   6*1 1064 3 6*0 2 1 1 2 1 1 1 2 1 fd5 8*0 ee5 9*1 114c 9*1 10f5 9*0 138c 8*0 126c 3 7*1 2 7*0 11dd
  //   7*1 1344 3 7*0 2 1 1 2 1 1 1 2 1 1 12a5 8*0 1195 9*1 142c 9*1 13d5 7*0 14f4 3 7*1 2 7*0 1465 7*1
  //   15c4 3 7*0 2 1 1 2 5*1 152d 9*0 15*2 1904 16e4 9*0 168d 2 0 170c 3 16f5 0 172c 3 1715 0 174c 3 1735
  //   0 176c 3 1755 0 178c 3 1775 0 17ac 3 1795 0 17cc 3 17b5 0 17ec 3 17d5 0 180c 3 17f5 9*1 18ac 9*1
  //   1855 9*0 3 1685 2 196c 0 2 8*0 190d 9*1 1a0c 9*1 19b5 9*0 204c 0 3 4*0 1aec 3 4*1 2 4*0 1a8d 4*1
  //   1d3c 3 4*0 2 5*1 1c9c 3 0 0 1bcc 3 1 1 2 0 0 1b8d 1 1 1c44 3 0 0 2 0 0 2 4*1 1bdd 2 9*0 1b6d 8*1
  //   1d34 9*1 1cdd 1b0d 9*0 1ddc 9*0 1d85 9*1 1f3c 0 1ee4 3 9*0 2 9*1 1e35 10*1 1e25 0 1ff4 3 9*0 2 9*1
  //   1f45 1 2 8*0 1a55 9*1 22ec 0 20bc 3 20a5 1 3 4*0 2224 3 4*1 2 0 21c4 1 3 0 3 6*1 2 6*0 212d 1 21fc 3
  //   0 2 1 21cd 4*0 20ed 1 1 1 228c 3 0 0 0 2 1 1 1 223d 1 2 9*1 2095 9*0 2394 0 2 8*0 2335 9*1 2434 9*1
  //   23dd 9*0 2ae4 0 3 5*0 252c 3 5*1 2 5*0 24bd 5*1 27b4 3 5*0 2 6*1 2714 3 0 0 0 263c 3 1 1 1 2 0 0 0
  //   25ed 1 1 1 26bc 3 0 0 0 2 0 2 4*1 2655 2 9*0 25c5 8*1 27ac 9*1 2755 2555 9*0 2854 9*0 27fd 9*1 29c4
  //   0 0 2964 3 9*0 2 9*1 28b5 11*1 289d 0 0 2a84 3 9*0 2 9*1 29d5 1 1 2 8*0 247d 9*1 2d84 0 2b54 3 2b3d
  //   1 3 4*0 2cbc 3 4*1 2 0 2c5c 1 3 0 3 6*1 2 6*0 2bc5 1 2c94 3 0 2 1 2c65 4*0 2b85 1 1 1 2d24 3 0 0 0 2
  //   1 1 1 2cd5 1 2 9*1 2b2d 9*0 3084 4*0 3054 3 36*1 2 36*0 2df5 5*0 2dcd 9*1 3124 9*1 30cd 9*0 15*2
  //   338c 3244 9*0 31ed 9*1 3 9*1 3334 9*1 32dd 9*0 3 31e5 2 21*0 2 1 1 1 34b4 9*1 345d 9*0 3c74 0 0 0
  //   356c 3 1 1 1 3 0 0 0 351d 2 1 1 1 3824 3 0 0 0 3 0 3624 3 4*1 2 4*0 35c5 4*1 381c 3 4*0 2 13*1 373c
  //   9*1 36e5 4*0 3774 3 375d 2 5*0 37fc 9*0 37a5 0 2 1 3645 358d 2 4*0 38ac 3 4*1 3 4*0 384d 2 4*1 3b64
  //   3 4*0 3 1 3964 3 1 1 1 2 0 0 0 3915 1 1 1 3b5c 3 0 0 0 2 12*1 3a64 9*1 3a0d 0 0 0 3a94 3 3a7d 2 6*0
  //   3b24 9*0 3acd 0 3b44 3 3b2d 2 1 397d 38d5 2 0 3c2c 3 1 3be4 9*0 3b8d 8*1 3b75 8*0 34fd 9*1 3d14 9*1
  //   3cbd 7*1 3db4 3 0 2 0 0 0 3 4*1 3d4d 9*0 26*2 0 0 3f3c 3 4*1 2 4*0 3edd 4*1 3fd4 3 4*0 2 1 1 3fbc 3
  //   3fa5 1 1 3f5d 0 0 152c 7*1 2 1 40ac 3 1 2 4*0 2 1 1 40a4 3 408d 4035 0 415c 3 1 1 413c 3 0 2 0 0 0 3
  //   4*1 40d5 0 0 0 40b5 13*0 4264 0 0 41f4 3 41dd 0 4214 3 41fd 0 4234 3 421d 5*0 41c5 9*1 4304 9*1 42ad
  //   0 0 0 4334 3 431d 6*0 44c4 5*0 43f4 3 4*1 2 4*0 4395 4*1 447c 3 4*0 2 1 1 1 2 1 4415 8*0 4365 9*1
  //   4564 9*1 450d 9*0 46b4 0 0 4674 3 9*1 2 9*0 45c5 7*0 45ad 9*1 4754 9*1 46fd 9*0 15*2 4a94 4874 9*0
  //   481d 2 0 489c 3 4885 0 48bc 3 48a5 0 48dc 3 48c5 0 48fc 3 48e5 0 491c 3 4905 0 493c 3 4925 0 495c 3
  //   4945 0 497c 3 4965 0 499c 3 4985 9*1 4a3c 9*1 49e5 9*0 3 4815 2 4afc 0 2 8*0 4a9d 9*1 4b9c 9*1 4b45
  //   9*0 51fc 0 3 5*0 4c94 3 5*1 2 5*0 4c25 5*1 4eec 3 5*0 2 6*1 4e4c 3 0 0 4d8c 3 1 1 2 0 0 4d4d 1 1
  //   4df4 3 0 0 2 0 2 1 1 1 4d9d 2 9*0 4d2d 8*1 4ee4 9*1 4e8d 4cbd 9*0 4f8c 9*0 4f35 9*1 50ec 0 5094 3
  //   9*0 2 9*1 4fe5 10*1 4fd5 0 51a4 3 9*0 2 9*1 50f5 1 2 8*0 4be5 9*1 547c 0 526c 3 5255 1 3 0 0 0 53cc
  //   3 1 1 1 2 0 5374 1 3 0 3 7*1 2 7*0 52cd 1 53ac 3 0 2 1 537d 0 0 0 5295 1 1 541c 3 0 0 2 1 1 53dd 1 2
  //   9*1 5245 9*0 5654 6*0 556c 3 5*1 2 5*0 54fd 5*1 560c 3 5*0 2 4*1 2 1 5595 8*0 54c5 9*1 56f4 9*1 569d
  //   9*0 579c 0 2 8*0 573d 9*1 583c 9*1 57e5 9*0 5eac 0 3 5*0 5934 3 5*1 2 5*0 58c5 5*1 5b9c 3 5*0 2 6*1
  //   5afc 3 0 0 5a2c 3 1 1 2 0 0 59ed 1 1 5aa4 3 0 0 2 0 0 2 4*1 5a3d 2 9*0 59cd 8*1 5b94 9*1 5b3d 595d
  //   9*0 5c3c 9*0 5be5 9*1 5d9c 0 5d44 3 9*0 2 9*1 5c95 10*1 5c85 0 5e54 3 9*0 2 9*1 5da5 1 2 8*0 5885
  //   9*1 614c 0 5f1c 3 5f05 1 3 4*0 6084 3 4*1 2 0 6024 1 3 0 3 6*1 2 6*0 5f8d 1 605c 3 0 2 1 602d 4*0
  //   5f4d 1 1 1 60ec 3 0 0 0 2 1 1 1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
endmodule
